# Fritzing sketch Cando2 (saved by Fritzing 0.8.7b)
circuit board: 8.46667cm x 5.64444cm
breadboards: 1

parts:
  Part1 = Arduino Uno (Rev3)
  R1 = PHOTOCELL [package=photocell-kit]
  R2 = PHOTOCELL [package=photocell-kit]
  R3 = PHOTOCELL [package=photocell-kit]
  R4 = PHOTOCELL [package=photocell-kit]
  R5 = PHOTOCELL [package=photocell-kit]
  J1 = Basic Servo
  J2 = Basic Servo
  Power_plug1 = Power plug
  R6 = Resistor [tolerance=±5% resistance=1k package="0603 [SMD]"]
  R7 = Resistor [tolerance=±5% resistance=1k package="0603 [SMD]"]
  R8 = Resistor [tolerance=±5% resistance=1k package="0603 [SMD]"]
  R9 = Resistor [tolerance=±5% resistance=1k package="0603 [SMD]"]
  R10 = Resistor [tolerance=±5% resistance=1k package="0603 [SMD]"]
  R11 = Resistor [tolerance=±5% resistance=10 package="0603 [SMD]"]
  C2 = Electrolytic Capacitor [capacitance=1μF package="0405 [SMD, electrolytic]"]
  C3 = Electrolytic Capacitor [capacitance=1μF package="0405 [SMD, electrolytic]"]
  R12 = Resistor [tolerance=±5% resistance=10 package="0603 [SMD]"]

nets:
  N1: Part1.A1, R5.P$1, R10.Pin_0
  N2: Part1.A2, R4.P$1, R9.Pin_0
  N3: Part1.A3, R3.P$1, R8.Pin_0
  N4: Part1.A4/SDA, R2.P$1, R7.Pin_0
  N5: Part1.A5/SCL, R1.P$1, R6.Pin_0
  N6: Part1.D6_PWM, J2.pulse
  N7: Part1.D7, J1.pulse
  GND: Part1.GND, J1.gnd, J2.gnd, Power_plug1.GND, R6.Pin_1, R7.Pin_1, R8.Pin_1, R9.Pin_1, R10.Pin_1
  VIN: Part1.VIN, R1.P$2, R2.P$2, R3.P$2, R4.P$2, R5.P$2, Power_plug1.VCC, R11.Pin_0, C2.+, C3.+, R12.Pin_0
  N8: J1.vcc, R11.Pin_1, C2.-
  N9: J2.vcc, C3.-, R12.Pin_1

notes:
  v2- better schematic coloring
